# Fritzing sketch Final Fritz Sketch (saved by Fritzing 0.9.3b)
breadboards: 1

parts:
  Part1 = Photon
  Adafruit_Atmega32u1 = Adafruit Atmega32u4 Breakout Board [part_number="Atmega 32u4"]
  Part6 = Arduino Uno (Rev3) - ICSP

nets:
  N1: Part1.RX, Adafruit_Atmega32u1.D0, Part6.D0/RX
  N2: Part1.TX, Adafruit_Atmega32u1.D1, Part6.D1/TX
  GND: Part1.GND, Adafruit_Atmega32u1.GND
